# Fritzing sketch ergosplit44 (saved by Fritzing 0.9.3b)

parts:
  A1 = Waveshare rp2040-zero tht extra conns [package=THT]
  S1 = Momentary Switch [package=ksa_sealed_tac_switch]
  S2 = Momentary Switch [package=ksa_sealed_tac_switch]
  S3 = Momentary Switch [package=ksa_sealed_tac_switch]
  S4 = Momentary Switch [package=ksa_sealed_tac_switch]
  S5 = Momentary Switch [package=ksa_sealed_tac_switch]
  S6 = Momentary Switch [package=ksa_sealed_tac_switch]
  S7 = Momentary Switch [package=ksa_sealed_tac_switch]
  S8 = Momentary Switch [package=ksa_sealed_tac_switch]
  S9 = Momentary Switch [package=ksa_sealed_tac_switch]
  S10 = Momentary Switch [package=ksa_sealed_tac_switch]
  S11 = Momentary Switch [package=ksa_sealed_tac_switch]
  S12 = Momentary Switch [package=ksa_sealed_tac_switch]
  S13 = Momentary Switch [package=ksa_sealed_tac_switch]
  S14 = Momentary Switch [package=ksa_sealed_tac_switch]
  S15 = Momentary Switch [package=ksa_sealed_tac_switch]
  S16 = Momentary Switch [package=ksa_sealed_tac_switch]
  S17 = Momentary Switch [package=ksa_sealed_tac_switch]
  S18 = Momentary Switch [package=ksa_sealed_tac_switch]
  S20 = Momentary Switch [package=ksa_sealed_tac_switch]
  S22 = Momentary Switch [package=ksa_sealed_tac_switch]
  S23 = Momentary Switch [package=ksa_sealed_tac_switch]
  S24 = Momentary Switch [package=ksa_sealed_tac_switch]
  S25 = Momentary Switch [package=ksa_sealed_tac_switch]
  S26 = Momentary Switch [package=ksa_sealed_tac_switch]
  S27 = Momentary Switch [package=ksa_sealed_tac_switch]
  S28 = Momentary Switch [package=ksa_sealed_tac_switch]
  S29 = Momentary Switch [package=ksa_sealed_tac_switch]
  S30 = Momentary Switch [package=ksa_sealed_tac_switch]
  S31 = Momentary Switch [package=ksa_sealed_tac_switch]
  S32 = Momentary Switch [package=ksa_sealed_tac_switch]
  S33 = Momentary Switch [package=ksa_sealed_tac_switch]
  S34 = Momentary Switch [package=ksa_sealed_tac_switch]
  S35 = Momentary Switch [package=ksa_sealed_tac_switch]
  S36 = Momentary Switch [package=ksa_sealed_tac_switch]
  S37 = Momentary Switch [package=ksa_sealed_tac_switch]
  S38 = Momentary Switch [package=ksa_sealed_tac_switch]
  S39 = Momentary Switch [package=ksa_sealed_tac_switch]
  S40 = Momentary Switch [package=ksa_sealed_tac_switch]
  S41 = Momentary Switch [package=ksa_sealed_tac_switch]
  S42 = Momentary Switch [package=ksa_sealed_tac_switch]
  S43 = Momentary Switch [package=ksa_sealed_tac_switch]
  S44 = Momentary Switch [package=ksa_sealed_tac_switch]
  S45 = Momentary Switch [package=ksa_sealed_tac_switch]
  S46 = Momentary Switch [package=ksa_sealed_tac_switch]

nets:
  N1: A1.Pin_8, S4.3, S11.3, S17.3, S23.3
  N2: A1.Pin_9, S3.3, S10.3, S16.3, S22.3
  N3: A1.Pin_10, S2.3, S8.3, S14.3, S20.3
  N4: A1.Pin_11, S1.3, S12.3, S18.3, S24.3
  N5: A1.Pin_12, S30.3, S36.3, S37.3, S46.3
  N6: A1.Pin_13, S27.3, S29.3, S33.3, S35.3
  N7: A1.Pin_14, S31.3, S40.3, S42.3, S45.3
  N8: A1.Pin_15, S26.3, S32.3, S39.3, S41.3
  N9: A1.Pin_16, S25.3, S28.3, S44.3
  N10: A1.Pin_17, S34.3, S38.3, S43.3
  N11: A1.Pin_18, S20.1, S22.1, S23.1, S24.1, S27.1, S32.1, S37.1, S45.1
  N12: A1.Pin_19, S13.1, S14.1, S15.1, S16.1, S17.1, S18.1, S25.1, S29.1, S34.1, S36.1, S39.1, S40.1
  N13: A1.Pin_20, S7.1, S8.1, S9.1, S10.1, S11.1, S12.1, S26.1, S35.1, S42.1, S43.1, S44.1, S46.1
  N14: A1.Pin_21, S1.1, S2.1, S3.1, S4.1, S5.1, S6.1, S28.1, S30.1, S31.1, S33.1, S38.1, S41.1
  N15: A1.Pin_24, S5.3, S9.3, S15.3
  N16: A1.Pin_25, S6.3, S7.3, S13.3

custom parts:
  Waveshare rp2040-zero tht extra conns: .RP2040-Zero, A Low-Cost, High-Performance Pico-Like MCU Board Based On Raspberry Pi Microcontroller RP2040. This varant is THT with the extra connections.
